// Logisim project JCPU.circ as structural Verilog: 6 circuits, main circuit JCPU
module JCPU (
);

  wire adc, add, afload, aload, aluop, \and , and_1_out, and_2_out, and_3_out, and_4_out, and_5_out,
       and_6_out, and_7_out, and_8_out, and_9_out, and_12_out, and_13_out, and_16_out, and_17_out,
       and_18_out, and_19_out, and_20_out, and_21_out, and_25_out, and_27_out, and_28_out, arg0load,
       arg1load, clock, comparator_1_eq, decoder_1_out2, decoder_1_out3, decoder_1_out4, decoder_1_out5,
       decoder_1_out6, demultiplexer_1_out1, demultiplexer_2_out0, demultiplexer_2_out1,
       demultiplexer_3_out0, demultiplexer_3_out1, demultiplexer_4_out0, devenable, enio0, enio1, enio2,
       enio3, ensph, enspl, fcarry, fload, irbit0, irbit1, irbit2, irbit3, irbit4, irbit5, irbit6, irbit7,
       irload, jnz, lc, lda, ldf, lw, lwa, multiplexer_1_out, mw, \nor , nor_1_out, nor_2_out, nor_3_out,
       not_1_out, not_2_out, not_3_out, not_4_out, not_5_out, nz, oenio0, oenio1, oenio2, oenio3, oensph,
       oenspl, op0, op1, \or , or_1_out, or_2_out, or_3_out, or_4_out, or_5_out, or_6_out, or_7_out,
       or_9_out, or_12_out, or_13_out, or_14_out, or_15_out, or_16_out, or_17_out, or_19_out, or_20_out,
       or_21_out, or_22_out, or_23_out, or_24_out, or_25_out, or_26_out, or_29_out, pcinc, pop, push,
       ramenable, reset, rload, romenable, rw, spldec, splinc, sw, swa, xload;
  wire [2:0] multiplexer_5_out, multiplexer_6_out, multiplexer_7_out, multiplexer_8_out, multiplexer_12_out,
       multiplexer_13_out, regsel0, regsel1;
  wire [3:0] alu_1_carry;
  wire [7:0] alu_1_out, arg0, arg1, controlled_buffer_1_out, controlled_buffer_2_out,
       controlled_buffer_10_out, devout, H, IO_0_q, IO_1_q, IO_2_q, IO_3_q, L, multiplexer_2_out,
       multiplexer_3_out, multiplexer_9_out, multiplexer_10_out, pc_adder_1_pch_out, pc_adder_1_pcl_out, PCh,
       PCl, Phase_Counter_q, ram_1_data, register_1_q, registers_1_out, rom_1_data, sph, spl;
  wire [14:0] ramaddr;
  wire [15:0] multiplexer_14_out, multiplexer_16_out;
  wire [15:15] romaddr;

  assign controlled_buffer_1_out = devenable ? devout : 8'bz;  // Controlled_Buffer controlled_buffer_1
  Register IO_0 (.D(controlled_buffer_2_out), .en(enio0), .Q(IO_0_q), .clk(clock));  // open: clr
  or or_1 (or_1_out, decoder_1_out6, demultiplexer_4_out0);
  not not_1 (not_1_out, rw);
  assign controlled_buffer_2_out = devenable ? multiplexer_10_out : 8'bz;  // Controlled_Buffer controlled_buffer_2
  assign devout = oenio0 ? IO_0_q : 8'bz;  // Controlled_Buffer controlled_buffer_3
  Counter Phase_Counter (
    .load(1'b0), .count(clock), .Q(Phase_Counter_q), .clk(clock), .clr(or_2_out));  // open: D, carry
  or or_2 (or_2_out, or_1_out, or_3_out);
  or or_3 (or_3_out, demultiplexer_3_out1, reset);
  or or_4 (or_4_out, sw, or_5_out);
  or or_5 (or_5_out, push, pop);
  ROM #(.addrWidth(16)) rom_1 (.addr({romaddr[15], ramaddr}), .data(rom_1_data), .sel(romenable));
  not not_2 (not_2_out, rw);
  RAM #(.addrWidth(16)) ram_1 (
    .addr({1'b0, ramaddr}), .data(ram_1_data), .sel(ramenable), .clk(clock), .ld(not_1_out));  // open: clr
  assign ram_1_data = rw ? multiplexer_10_out : 8'bz;  // Controlled_Buffer controlled_buffer_4
  assign devout = oenio1 ? IO_1_q : 8'bz;  // Controlled_Buffer controlled_buffer_5
  Register IO_1 (.D(controlled_buffer_2_out), .en(enio1), .Q(IO_1_q), .clk(clock));  // open: clr
  Decoder #(.select(3), .enable("false")) decoder_1 (
    .out0(irload), .out1(arg0load), .out2(decoder_1_out2), .out3(decoder_1_out3), .out4(decoder_1_out4),
    .out5(decoder_1_out5), .out6(decoder_1_out6), .sel(Phase_Counter_q[2:0]));  // open: out7
  or or_6 (or_6_out, lw, or_4_out);
  and and_1 (and_1_out, ramenable, not_2_out);
  assign controlled_buffer_1_out = and_1_out ? ram_1_data : 8'bz;  // Controlled_Buffer controlled_buffer_6
  Register IO_2 (.D(controlled_buffer_2_out), .en(enio2), .Q(IO_2_q), .clk(clock));  // open: clr
  or or_7 (or_7_out, jnz, or_6_out);
  assign controlled_buffer_1_out = romenable ? rom_1_data : 8'bz;  // Controlled_Buffer controlled_buffer_7
  Register IR (
    .D(controlled_buffer_1_out), .en(irload),
    .Q({irbit7, irbit6, irbit5, irbit4, irbit3, irbit2, irbit1, irbit0}), .clk(clock));  // open: clr
  Register u_ARG0 (.D(controlled_buffer_1_out), .en(arg0load), .Q(arg0), .clk(clock));  // open: clr
  Register u_ARG1 (.D(controlled_buffer_1_out), .en(arg1load), .Q(arg1), .clk(clock));  // open: clr
  assign devout = oenio2 ? IO_2_q : 8'bz;  // Controlled_Buffer controlled_buffer_8
  or or_8 (pcinc, arg1load, or_9_out);
  or or_9 (or_9_out, arg0load, irload);
  Demultiplexer #(.enable("false")) demultiplexer_1 (
    .out0(arg1load), .out1(demultiplexer_1_out1), .in(decoder_1_out2), .sel(or_7_out));
  Demultiplexer #(.enable("false")) demultiplexer_2 (
    .out0(demultiplexer_2_out0), .out1(demultiplexer_2_out1), .in(decoder_1_out3), .sel(or_7_out));
  Demultiplexer #(.enable("false")) demultiplexer_3 (
    .out0(demultiplexer_3_out0), .out1(demultiplexer_3_out1), .in(decoder_1_out4), .sel(or_7_out));
  Register IO_3 (.D(controlled_buffer_2_out), .en(enio3), .Q(IO_3_q), .clk(clock));  // open: clr
  Multiplexer #(.enable("false")) multiplexer_1 (.in0(or_14_out), .in1(1'b0), .out(multiplexer_1_out), .sel(enspl));
  or or_10 (op0, demultiplexer_1_out1, demultiplexer_2_out0);
  or or_11 (op1, demultiplexer_2_out1, demultiplexer_3_out0);
  and and_2 (and_2_out, and_3_out, not_3_out);
  not not_3 (not_3_out, pcinc);
  Multiplexer #(.width(8), .enable("false")) multiplexer_2 (
    .in0(pc_adder_1_pch_out), .in1(H), .out(multiplexer_2_out), .sel(and_2_out));
  Multiplexer #(.width(8), .enable("false")) multiplexer_3 (
    .in0(pc_adder_1_pcl_out), .in1(L), .out(multiplexer_3_out), .sel(and_2_out));
  or or_12 (or_12_out, and_2_out, pcinc);
  assign devout = oenio3 ? IO_3_q : 8'bz;  // Controlled_Buffer controlled_buffer_9
  Counter BPL (
    .load(or_13_out), .D(controlled_buffer_2_out), .count(multiplexer_1_out), .Q(spl), .clk(clock));  // open: carry, clr
  or or_13 (or_13_out, spldec, enspl);
  or or_14 (or_14_out, spldec, splinc);
  Demultiplexer #(.enable("false")) demultiplexer_4 (
    .out0(demultiplexer_4_out0), .out1(afload), .in(decoder_1_out5), .sel(or_15_out));
  or or_15 (or_15_out, add, adc);
  and and_3 (and_3_out, nz, jnz);
  Register u_PCh (.D(multiplexer_2_out), .en(or_12_out), .Q(PCh), .clk(clock));  // open: clr
  Register u_PCl (.D(multiplexer_3_out), .en(or_12_out), .Q(PCl), .clk(clock));  // open: clr
  assign controlled_buffer_10_out = rload ? controlled_buffer_1_out : 8'bz;  // Controlled_Buffer controlled_buffer_10
  assign devout = oenspl ? spl : 8'bz;  // Controlled_Buffer controlled_buffer_11
  PC_Adder pc_adder_1 (.PCh(PCh), .PCl(PCl), .PCh_Out(pc_adder_1_pch_out), .PCl_Out(pc_adder_1_pcl_out));
  and and_4 (and_4_out, lda, op0);
  assign controlled_buffer_10_out = and_4_out ? arg0 : 8'bz;  // Controlled_Buffer controlled_buffer_12
  assign controlled_buffer_10_out = and_5_out ? multiplexer_10_out : 8'bz;  // Controlled_Buffer controlled_buffer_13
  and and_5 (and_5_out, mw, op0);
  assign devout = oensph ? sph : 8'bz;  // Controlled_Buffer controlled_buffer_14
  Register BPH (.D(controlled_buffer_2_out), .en(ensph), .Q(sph), .clk(clock));  // open: clr
  nor nor_1 (nor_1_out, push, pop);
  nor nor_2 (nor_2_out, aluop, ldf);
  or or_16 (or_16_out, \nor , or_17_out);
  or or_17 (or_17_out, \and , adc);
  assign controlled_buffer_10_out = aload ? alu_1_out : 8'bz;  // Controlled_Buffer controlled_buffer_15
  and and_6 (and_6_out, nor_1_out, nor_2_out);
  or or_18 (aluop, add, or_19_out);
  or or_19 (or_19_out, \or , or_16_out);
  Multiplexer #(.width(3), .enable("false")) multiplexer_4 (
    .in0(multiplexer_5_out), .in1(3'b111), .out(regsel0), .sel(ldf));
  Multiplexer #(.width(3), .enable("false")) multiplexer_5 (
    .in0(multiplexer_6_out), .in1(arg1[2:0]), .out(multiplexer_5_out), .sel(mw));
  Multiplexer #(.width(3), .enable("false")) multiplexer_6 (
    .in0(arg0[2:0]), .in1(multiplexer_7_out), .out(multiplexer_6_out), .sel(lda));
  Multiplexer #(.width(3), .enable("false")) multiplexer_7 (
    .in0({irbit6, irbit5, irbit4}), .in1(multiplexer_8_out), .out(multiplexer_7_out), .sel(lwa));
  Multiplexer #(.width(3), .enable("false")) multiplexer_8 (
    .in0(3'b010), .in1(3'b011), .out(multiplexer_8_out), .sel(op1));
  and and_7 (and_7_out, lda, op1);
  or or_20 (or_20_out, and_7_out, and_8_out);
  assign controlled_buffer_10_out = or_20_out ? arg1 : 8'bz;  // Controlled_Buffer controlled_buffer_16
  and and_8 (and_8_out, lc, op0);
  assign controlled_buffer_10_out = fload ? {4'b0000, alu_1_carry} : 8'bz;  // Controlled_Buffer controlled_buffer_17
  and and_9 (and_9_out, fcarry, adc);
  and and_10 (devenable, and_13_out, romaddr[15]);
  and and_11 (reset, and_6_out, op1);
  Clock clock_1 (.out(clock));
  ALU alu_1 (
    .X(register_1_q), .Y(multiplexer_10_out), .Cin(and_9_out), .Op0(irbit0), .Op1(irbit1),
    .Carry(alu_1_carry[0]), .Greater_Than(alu_1_carry[1]), .Equal(alu_1_carry[2]),
    .Less_Than(alu_1_carry[3]), .Out(alu_1_out));
  and and_12 (and_12_out, and_17_out, ramaddr[13]);
  and and_13 (and_13_out, and_12_out, ramaddr[14]);
  Registers registers_1 (
    .Clock(clock), .L(L), .H(H), .Out(registers_1_out), .oregsel(regsel1), .In(controlled_buffer_10_out),
    .iregsel(regsel0), .Carry(fcarry));
  Register register_1 (.D(multiplexer_10_out), .en(xload), .Q(register_1_q), .clk(clock));  // open: clr
  and and_14 (ramenable, not_4_out, romaddr[15]);
  and and_15 (romenable, not_4_out, not_5_out);
  not not_4 (not_4_out, devenable);
  and and_16 (and_16_out, and_21_out, ramaddr[11]);
  and and_17 (and_17_out, and_16_out, ramaddr[12]);
  or or_21 (or_21_out, aluop, ldf);
  and and_18 (and_18_out, irbit7, sw);
  Multiplexer #(.width(8), .enable("false")) multiplexer_9 (
    .in0(arg1), .in1(arg0), .out(multiplexer_9_out), .sel(and_18_out));
  and and_19 (and_19_out, irbit7, or_25_out);
  Multiplexer #(.width(8), .enable("false")) multiplexer_10 (
    .in0(registers_1_out), .in1(multiplexer_9_out), .out(multiplexer_10_out), .sel(and_19_out));
  not not_5 (not_5_out, romaddr[15]);
  and and_20 (and_20_out, ramaddr[8], ramaddr[9]);
  and and_21 (and_21_out, and_20_out, ramaddr[10]);
  Decoder #(.select(4), .enable("false")) decoder_2 (
    .out0(lw), .out1(sw), .out2(lda), .out3(lc), .out4(add), .out5(\or ), .out6(\nor ), .out7(\and ),
    .out8(jnz), .out9(mw), .out10(ldf), .out11(lwa), .out12(adc), .out13(swa), .out14(push), .out15(pop),
    .sel({irbit3, irbit2, irbit1, irbit0}));
  Multiplexer #(.width(3), .enable("false")) multiplexer_11 (
    .in0(multiplexer_12_out), .in1(multiplexer_13_out), .out(regsel1), .sel(or_22_out));
  or or_22 (or_22_out, aluop, ldf);
  Multiplexer #(.width(3), .enable("false")) multiplexer_12 (
    .in0(arg0[2:0]), .in1({irbit6, irbit5, irbit4}), .out(multiplexer_12_out), .sel(swa));
  and and_22 (xload, or_21_out, op0);
  and and_23 (aload, aluop, op1);
  or or_23 (or_23_out, push, swa);
  or or_24 (or_24_out, or_23_out, sw);
  or or_25 (or_25_out, op1, jnz);
  not not_6 (nz, comparator_1_eq);
  Comparator comparator_1 (.a({8{1'b0}}), .b(multiplexer_10_out), .eq(comparator_1_eq));  // open: gt, lt
  Multiplexer #(.width(3), .enable("false")) multiplexer_13 (
    .in0(arg0[2:0]), .in1(arg1[2:0]), .out(multiplexer_13_out), .sel(op1));
  and and_24 (rw, or_24_out, op0);
  Decoder #(.select(3), .enable("false")) decoder_3 (
    .out0(oenio0), .out1(oenio1), .out2(oenio2), .out3(oenio3), .out4(oenspl), .out5(oensph),
    .sel(ramaddr[2:0]));  // open: out6, out7
  and and_25 (and_25_out, ldf, op1);
  and and_26 (spldec, push, op1);
  and and_27 (and_27_out, lw, op0);
  and and_28 (and_28_out, pop, op1);
  and and_29 (splinc, pop, op0);
  or or_26 (or_26_out, lwa, swa);
  Multiplexer #(.width(16), .enable("false")) multiplexer_14 (
    .in0(multiplexer_16_out), .in1({arg0, arg1}), .out(multiplexer_14_out), .sel(or_26_out));
  Multiplexer #(.width(16), .enable("false")) multiplexer_15 (
    .in0(multiplexer_14_out), .in1({PCh, PCl}), .out({romaddr[15], ramaddr}), .sel(nor_3_out));
  nor nor_3 (nor_3_out, op0, op1);
  or or_27 (fload, and_25_out, afload);
  or or_28 (rload, and_27_out, and_28_out);
  or or_29 (or_29_out, push, pop);
  Multiplexer #(.width(16), .enable("false")) multiplexer_16 (
    .in0({H, L}), .in1({sph, spl}), .out(multiplexer_16_out), .sel(or_29_out));
  and and_30 (enio0, oenio0, rw);
  and and_31 (enio1, oenio1, rw);
  and and_32 (enio2, oenio2, rw);
  and and_33 (enio3, oenio3, rw);
  and and_34 (enspl, oenspl, rw);
  and and_35 (ensph, oensph, rw);

  // Other names for the same wires on the sheet: romaddr[14:0] = ramaddr

  // Notes on the sheet:
  //   contents of rom_1 (hex, n*v repeats v):
  //   3 6 80 6d ff 5 3 6 ff 6d ff 4 e 6 f
endmodule

module _3_Bit_Dmux (
  input  [7:0] in_1,
  input  [2:0] Sel,
  output [7:0] out_3,
  output [7:0] out_4,
  output [7:0] out_5,
  output [7:0] out_6,
  output [7:0] out_7,
  output [7:0] out_8,
  output [7:0] out_9,
  output [7:0] out_10
);

  wire and_1_out, and_2_out, and_3_out, and_4_out, and_5_out, and_6_out, and_7_out, and_8_out, and_9_out,
       and_10_out, nor_1_out, nor_2_out, not_1_out, not_2_out, not_3_out, not_4_out, not_5_out, or_1_out,
       or_2_out;

  assign out_3 = nor_1_out ? in_1 : 8'bz;  // Controlled_Buffer controlled_buffer_1
  nor nor_1 (nor_1_out, or_1_out, Sel[0]);
  nor nor_2 (nor_2_out, Sel[2], Sel[1]);
  or or_1 (or_1_out, Sel[2], Sel[1]);
  assign out_5 = and_1_out ? in_1 : 8'bz;  // Controlled_Buffer controlled_buffer_2
  assign out_4 = and_2_out ? in_1 : 8'bz;  // Controlled_Buffer controlled_buffer_3
  and and_1 (and_1_out, and_3_out, not_2_out);
  and and_2 (and_2_out, nor_2_out, Sel[0]);
  and and_3 (and_3_out, not_1_out, Sel[1]);
  not not_1 (not_1_out, Sel[2]);
  not not_2 (not_2_out, Sel[0]);
  assign out_6 = and_4_out ? in_1 : 8'bz;  // Controlled_Buffer controlled_buffer_4
  and and_4 (and_4_out, and_3_out, Sel[0]);
  and and_5 (and_5_out, not_3_out, Sel[2]);
  not not_3 (not_3_out, or_2_out);
  or or_2 (or_2_out, Sel[0], Sel[1]);
  assign out_7 = and_5_out ? in_1 : 8'bz;  // Controlled_Buffer controlled_buffer_5
  and and_6 (and_6_out, and_7_out, not_4_out);
  and and_7 (and_7_out, Sel[0], Sel[2]);
  assign out_9 = and_8_out ? in_1 : 8'bz;  // Controlled_Buffer controlled_buffer_6
  assign out_8 = and_6_out ? in_1 : 8'bz;  // Controlled_Buffer controlled_buffer_7
  and and_8 (and_8_out, and_9_out, not_5_out);
  not not_4 (not_4_out, Sel[1]);
  not not_5 (not_5_out, Sel[0]);
  and and_9 (and_9_out, Sel[1], Sel[2]);
  assign out_10 = and_10_out ? in_1 : 8'bz;  // Controlled_Buffer controlled_buffer_8
  and and_10 (and_10_out, and_9_out, Sel[0]);
endmodule

module _3_Bit_Mux (
  input  [7:0] in_1,
  input  [7:0] in_2,
  input  [7:0] in_3,
  input  [7:0] in_4,
  input  [7:0] in_5,
  input  [7:0] in_6,
  input  [7:0] in_7,
  input  [7:0] in_8,
  input  [2:0] Sel,
  output [7:0] out_10
);

  wire and_1_out, and_2_out, and_3_out, and_4_out, and_5_out, and_6_out, and_7_out, and_8_out, and_9_out,
       and_10_out, nor_1_out, nor_2_out, not_1_out, not_2_out, not_3_out, not_4_out, not_5_out, or_1_out,
       or_2_out;

  assign out_10 = nor_1_out ? in_1 : 8'bz;  // Controlled_Buffer controlled_buffer_1
  nor nor_1 (nor_1_out, or_1_out, Sel[0]);
  or or_1 (or_1_out, Sel[2], Sel[1]);
  assign out_10 = and_1_out ? in_2 : 8'bz;  // Controlled_Buffer controlled_buffer_2
  and and_1 (and_1_out, nor_2_out, Sel[0]);
  and and_2 (and_2_out, and_3_out, not_2_out);
  and and_3 (and_3_out, not_1_out, Sel[1]);
  nor nor_2 (nor_2_out, Sel[2], Sel[1]);
  not not_1 (not_1_out, Sel[2]);
  assign out_10 = and_4_out ? in_4 : 8'bz;  // Controlled_Buffer controlled_buffer_3
  assign out_10 = and_2_out ? in_3 : 8'bz;  // Controlled_Buffer controlled_buffer_4
  and and_4 (and_4_out, and_3_out, Sel[0]);
  not not_2 (not_2_out, Sel[0]);
  assign out_10 = and_5_out ? in_5 : 8'bz;  // Controlled_Buffer controlled_buffer_5
  and and_5 (and_5_out, not_3_out, Sel[2]);
  not not_3 (not_3_out, or_2_out);
  or or_2 (or_2_out, Sel[0], Sel[1]);
  assign out_10 = and_7_out ? in_7 : 8'bz;  // Controlled_Buffer controlled_buffer_6
  assign out_10 = and_6_out ? in_6 : 8'bz;  // Controlled_Buffer controlled_buffer_7
  and and_6 (and_6_out, and_9_out, not_4_out);
  and and_7 (and_7_out, and_8_out, not_5_out);
  not not_4 (not_4_out, Sel[1]);
  not not_5 (not_5_out, Sel[0]);
  and and_8 (and_8_out, Sel[1], Sel[2]);
  and and_9 (and_9_out, Sel[0], Sel[2]);
  assign out_10 = and_10_out ? in_8 : 8'bz;  // Controlled_Buffer controlled_buffer_8
  and and_10 (and_10_out, and_8_out, Sel[0]);
endmodule

module Registers (
  input  Clock,
  input  [7:0] In,
  input  [2:0] oregsel,
  input  [2:0] iregsel,
  output [7:0] L,
  output [7:0] H,
  output [7:0] Out,
  output Carry
);

  wire aen, ben, cen, den, een, fen, hen, len;
  wire [7:0] A_q, B_q, C_q, D_q, E_q;
  wire [7:1] F_q;

  Decoder #(.select(3), .enable("false")) decoder_1 (
    .out0(ben), .out1(cen), .out2(hen), .out3(len), .out4(den), .out5(een), .out6(aen), .out7(fen),
    .sel(iregsel));
  Register B (.D(In), .en(ben), .Q(B_q), .clk(Clock));  // open: clr
  Register C (.D(In), .en(cen), .Q(C_q), .clk(Clock));  // open: clr
  Register u_H (.D(In), .en(hen), .Q(H), .clk(Clock));  // open: clr
  Register u_L (.D(In), .en(len), .Q(L), .clk(Clock));  // open: clr
  Register D (.D(In), .en(den), .Q(D_q), .clk(Clock));  // open: clr
  Register E (.D(In), .en(een), .Q(E_q), .clk(Clock));  // open: clr
  Register A (.D(In), .en(aen), .Q(A_q), .clk(Clock));  // open: clr
  Register F (.D(In), .en(fen), .Q({F_q, Carry}), .clk(Clock));  // open: clr
  _3_Bit_Mux u_3_bit_mux_1 (
    .in_1(B_q), .in_2(C_q), .in_3(H), .in_4(L), .in_5(D_q), .in_6(E_q), .in_7(A_q), .in_8({F_q, Carry}),
    .Sel(oregsel), .out_10(Out));
endmodule

module ALU (
  input  Cin,
  input  Op0,
  input  Op1,
  input  [7:0] X,
  input  [7:0] Y,
  output [7:0] Out,
  output Carry,
  output Greater_Than,
  output Equal,
  output Less_Than
);

  wire decoder_1_out0, decoder_1_out1, decoder_1_out2, decoder_1_out3;
  wire [7:0] adder_1_out, and_1_out, nor_1_out, or_1_out;

  Decoder #(.select(2), .enable("false")) decoder_1 (
    .out0(decoder_1_out0), .out1(decoder_1_out1), .out2(decoder_1_out2), .out3(decoder_1_out3),
    .sel({Op1, Op0}));
  Adder adder_1 (.a(X), .b(Y), .out(adder_1_out), .cin(Cin), .cout(Carry));
  assign nor_1_out = ~(X | Y);  // NOR_Gate nor_1, 8 bits wide
  assign and_1_out = X & Y;  // AND_Gate and_1, 8 bits wide
  assign or_1_out = X | Y;  // OR_Gate or_1, 8 bits wide
  Comparator comparator_1 (.a(X), .b(Y), .gt(Greater_Than), .eq(Equal), .lt(Less_Than));
  assign Out = decoder_1_out0 ? adder_1_out : 8'bz;  // Controlled_Buffer controlled_buffer_1
  assign Out = decoder_1_out2 ? nor_1_out : 8'bz;  // Controlled_Buffer controlled_buffer_2
  assign Out = decoder_1_out3 ? and_1_out : 8'bz;  // Controlled_Buffer controlled_buffer_3
  assign Out = decoder_1_out1 ? or_1_out : 8'bz;  // Controlled_Buffer controlled_buffer_4
endmodule

module PC_Adder (
  input  [7:0] PCh,
  input  [7:0] PCl,
  output [7:0] PCh_Out,
  output [7:0] PCl_Out
);

  Adder #(.width(16)) adder_1 (.a({PCh, PCl}), .b(16'h1), .out({PCh_Out, PCl_Out}));  // open: cin, cout
endmodule
